// Logisim project 1.circ as structural Verilog: 2 circuits, main circuit ods1bit
module ods1bit (
  input  A,
  input  S,
  input  B,
  input  Cout,
  input  Cin
);

  wire not_1_out, not_2_out, not_3_out, or_1_out, or_2_out, or_3_out, or_4_out, or_5_out, or_6_out, or_7_out;

  not not_1 (not_1_out, A);
  not not_2 (not_2_out, B);
  not not_3 (not_3_out, Cin);
  or or_1 (or_1_out, A, B, Cin);
  or or_2 (or_2_out, A, not_2_out, not_3_out);
  or or_3 (or_3_out, not_1_out, B, not_3_out);
  or or_4 (or_4_out, not_1_out, not_2_out, Cin);
  or or_5 (or_5_out, A, B, not_3_out);
  or or_6 (or_6_out, A, not_2_out, Cin);
  or or_7 (or_7_out, not_1_out, B, Cin);
  and and_1 (S, or_1_out, or_2_out, or_3_out, or_4_out);
  and and_2 (Cout, or_5_out, or_6_out, or_7_out);
endmodule

module ODS8bit (
  input  [7:0] A,
  input  Overflow,
  input  [7:0] S,
  input  [7:0] B
);

  wire ods1bit_5_p2;

  // ods1bit ods1bit_1: pin names not known; wires that end beside it: S[7], Overflow
  ods1bit ods1bit_2 (.S(S[6]));  // open: A, B, Cin, Cout
  ods1bit ods1bit_3 (.S(S[5]));  // open: A, B, Cin, Cout
  ods1bit ods1bit_4 (.S(S[4]));  // open: A, B, Cin, Cout
  // ods1bit ods1bit_5: pin names not known; wires that end beside it: S[3], ods1bit_5_p2
  ods1bit ods1bit_6 (.S(S[2]));  // open: A, B, Cin, Cout
  ods1bit ods1bit_7 (.S(S[1]));  // open: A, B, Cin, Cout
  ods1bit ods1bit_8 (.S(S[0]));  // open: A, B, Cin, Cout
endmodule
