// Logisim project 3.circ as structural Verilog: 1 circuit, main circuit main
module main (
  input  in_1,
  input  in_2,
  input  in_3
);

  wire and_1_out, not_1_out, t_ff_1_p2, t_ff_2_p2;

  and and_1 (and_1_out, t_ff_2_p2, not_1_out);
  // T_Flip_Flop t_ff_1: pin names not known; wires that end beside it: and_1_out, t_ff_1_p2
  Clock clock_1 (.out(t_ff_1_p2));
  not not_1 (not_1_out, in_2);
  // T_Flip_Flop t_ff_2: pin names not known; wires that end beside it: in_1, t_ff_2_p2, t_ff_1_p2
  not not_2 (t_ff_2_p2, in_3);
  // T_Flip_Flop t_ff_3: pin names not known; wires that end beside it: in_2, in_2, 1'b1, t_ff_1_p2
endmodule
